// Logisim project circuito-v4-4.circ as structural Verilog: 6 circuits, main circuit main
module main (
  input  [7:0] in_1,
  input  in_2,
  output [7:0] out_3
);

  wire and_1_out, clock_1_out, controle_1_load, controle_1_shift, n74ls165_1_q, n74ls595_1_a, n74ls595_1_b,
       n74ls595_1_c, n74ls595_1_d, n74ls595_1_e, n74ls595_1_f, n74ls595_1_g, n74ls595_1_h;

  Clock clock_1 (.out(clock_1_out));
  _74LS165 u_74ls165_1 (
    .SER(1'b0), .CLK(clock_1_out), .CLK_INH(1'b0), .SH_nLD(in_2), .Q(n74ls165_1_q), .A(in_1[7]), .B(in_1[6]),
    .C(in_1[5]), .D(in_1[4]), .E(in_1[3]), .F(in_1[2]), .G(in_1[1]), .H(in_1[0]));  // open: nQ
  Pull_Resistor pull_resistor_1 (.node(n74ls165_1_q));
  CONTROLE controle_1 (.CLK(clock_1_out), .IN(and_1_out), .LOAD(controle_1_load), .SHIFT(controle_1_shift));
  and and_1 (and_1_out, in_2, n74ls165_1_q);
  LED led_1 (.in(controle_1_load));
  Shift_Register shift_register_1 (
    .shift(1'b1), .in(and_1_out), .clk(controle_1_shift), .q0(out_3[7]), .q1(out_3[6]), .q2(out_3[5]),
    .q3(out_3[4]), .q4(out_3[3]), .q5(out_3[2]), .q6(out_3[1]), .q7(out_3[0]));  // open: out, load, clr, d0, d1, d2, d3, d4, d5, d6, d7
  _74LS595 u_74ls595_1 (
    .nOE(1'b0), .RCLK(controle_1_load), .SRCLK(controle_1_shift), .nSRCLR(1'b1), .SER(and_1_out),
    .A(n74ls595_1_a), .B(n74ls595_1_b), .C(n74ls595_1_c), .D(n74ls595_1_d), .E(n74ls595_1_e),
    .F(n74ls595_1_f), .G(n74ls595_1_g), .H(n74ls595_1_h));  // open: nH
  // Probe on n74ls595_1_a
  // Probe on n74ls595_1_b
  // Probe on n74ls595_1_c
  // Probe on n74ls595_1_d
  // Probe on n74ls595_1_e
  // Probe on n74ls595_1_f
  // Probe on n74ls595_1_g
  // Probe on n74ls595_1_h
endmodule

module CONTROLE (
  input  CLK,
  input  IN,
  output SHIFT,
  output LOAD
);

  wire A, B, C, D, d_ff_1_qn, d_ff_2_qn, d_ff_3_qn, d_ff_4_qn, or_1_out;
  wire [7:1] rom_1_data;

  Pull_Resistor pull_resistor_1 (.node(IN));
  or or_1 (or_1_out, CLK, rom_1_data[2]);
  D_Flip_Flop d_ff_1 (.clk(or_1_out), .D(d_ff_1_qn), .Q(D), .Qn(d_ff_1_qn), .reset(rom_1_data[3]));  // open: preset, en
  D_Flip_Flop d_ff_2 (
    .clk(d_ff_1_qn), .D(d_ff_2_qn), .Q(C), .Qn(d_ff_2_qn), .reset(rom_1_data[3]));  // open: preset, en
  ROM rom_1 (.addr({3'b000, A, B, C, D, IN}), .data({rom_1_data, LOAD}));  // open: sel
  D_Flip_Flop d_ff_3 (
    .clk(d_ff_2_qn), .D(d_ff_3_qn), .Q(B), .Qn(d_ff_3_qn), .reset(rom_1_data[3]));  // open: preset, en
  D_Flip_Flop d_ff_4 (
    .clk(d_ff_3_qn), .D(d_ff_4_qn), .Q(A), .Qn(d_ff_4_qn), .reset(rom_1_data[3]));  // open: preset, en
  or or_2 (SHIFT, CLK, rom_1_data[1]);

  // Other names for the same wires on the sheet: E = IN

  // Notes on the sheet:
  //   contents of rom_1 (hex, n*v repeats v):
  //   6 15*0 3 3 e e
endmodule

module EDGE (
  input  IN,
  output OUT
);

  wire not_1_out, not_2_out, not_3_out;

  Pull_Resistor pull_resistor_1 (.node(IN));
  not not_1 (not_1_out, IN);
  not not_2 (not_2_out, not_1_out);
  and and_1 (OUT, IN, not_3_out);
  not not_3 (not_3_out, not_2_out);
endmodule

module _74LS165 (
  input  A,
  input  B,
  input  C,
  input  D,
  input  E,
  input  F,
  input  G,
  input  H,
  input  SER,
  input  CLK,
  input  CLK_INH,
  input  SH_nLD,
  output Q,
  output nQ
);

  wire and_1_out, and_2_out, and_3_out, and_4_out, and_5_out, and_6_out, and_7_out, and_8_out, and_9_out,
       and_10_out, and_11_out, and_12_out, and_13_out, and_14_out, and_15_out, and_16_out, and_17_out,
       and_18_out, nor_1_out, not_1_out, not_2_out, not_3_out, not_4_out, not_5_out, not_6_out, not_7_out,
       not_8_out, not_9_out, not_10_out, not_11_out, sr_m_s_1_nq, sr_m_s_1_q, sr_m_s_2_nq, sr_m_s_2_q,
       sr_m_s_3_nq, sr_m_s_3_q, sr_m_s_4_nq, sr_m_s_4_q, sr_m_s_5_nq, sr_m_s_5_q, sr_m_s_6_nq, sr_m_s_6_q,
       sr_m_s_7_nq, sr_m_s_7_q;

  not not_1 (not_1_out, SH_nLD);
  not not_2 (not_2_out, SER);
  not not_3 (not_3_out, not_2_out);
  and and_1 (and_1_out, CLK, SH_nLD);
  nor nor_1 (nor_1_out, and_1_out, and_2_out);
  and and_2 (and_2_out, CLK_INH, SH_nLD);
  SR_M_S sr_m_s_1 (
    .S(not_3_out), .CLK(nor_1_out), .R(not_2_out), .P(and_3_out), ._0(and_4_out), .Q(sr_m_s_1_q),
    .nQ(sr_m_s_1_nq));
  not not_4 (not_4_out, and_3_out);
  and and_3 (and_3_out, A, not_1_out);
  SR_M_S sr_m_s_2 (
    .S(sr_m_s_1_q), .CLK(nor_1_out), .R(sr_m_s_1_nq), .P(and_5_out), ._0(and_6_out), .Q(sr_m_s_2_q),
    .nQ(sr_m_s_2_nq));
  and and_4 (and_4_out, not_4_out, not_1_out);
  not not_5 (not_5_out, and_5_out);
  and and_5 (and_5_out, B, not_1_out);
  SR_M_S sr_m_s_3 (
    .S(sr_m_s_2_q), .CLK(nor_1_out), .R(sr_m_s_2_nq), .P(and_7_out), ._0(and_8_out), .Q(sr_m_s_3_q),
    .nQ(sr_m_s_3_nq));
  and and_6 (and_6_out, not_5_out, not_1_out);
  not not_6 (not_6_out, and_7_out);
  and and_7 (and_7_out, C, not_1_out);
  SR_M_S sr_m_s_4 (
    .S(sr_m_s_3_q), .CLK(nor_1_out), .R(sr_m_s_3_nq), .P(and_9_out), ._0(and_10_out), .Q(sr_m_s_4_q),
    .nQ(sr_m_s_4_nq));
  and and_8 (and_8_out, not_6_out, not_1_out);
  not not_7 (not_7_out, and_9_out);
  and and_9 (and_9_out, D, not_1_out);
  SR_M_S sr_m_s_5 (
    .S(sr_m_s_4_q), .CLK(nor_1_out), .R(sr_m_s_4_nq), .P(and_11_out), ._0(and_12_out), .Q(sr_m_s_5_q),
    .nQ(sr_m_s_5_nq));
  and and_10 (and_10_out, not_7_out, not_1_out);
  not not_8 (not_8_out, and_11_out);
  and and_11 (and_11_out, E, not_1_out);
  SR_M_S sr_m_s_6 (
    .S(sr_m_s_5_q), .CLK(nor_1_out), .R(sr_m_s_5_nq), .P(and_13_out), ._0(and_14_out), .Q(sr_m_s_6_q),
    .nQ(sr_m_s_6_nq));
  and and_12 (and_12_out, not_8_out, not_1_out);
  not not_9 (not_9_out, and_13_out);
  and and_13 (and_13_out, F, not_1_out);
  SR_M_S sr_m_s_7 (
    .S(sr_m_s_6_q), .CLK(nor_1_out), .R(sr_m_s_6_nq), .P(and_15_out), ._0(and_16_out), .Q(sr_m_s_7_q),
    .nQ(sr_m_s_7_nq));
  and and_14 (and_14_out, not_9_out, not_1_out);
  not not_10 (not_10_out, and_15_out);
  and and_15 (and_15_out, G, not_1_out);
  SR_M_S sr_m_s_8 (.S(sr_m_s_7_q), .CLK(nor_1_out), .R(sr_m_s_7_nq), .P(and_17_out), ._0(and_18_out), .Q(Q), .nQ(nQ));
  and and_16 (and_16_out, not_10_out, not_1_out);
  not not_11 (not_11_out, and_17_out);
  and and_17 (and_17_out, H, not_1_out);
  and and_18 (and_18_out, not_11_out, not_1_out);
endmodule

module SR_M_S (
  input  S,
  input  CLK,
  input  R,
  input  P,
  input  _0,
  output Q,
  output nQ
);

  wire not_1_out, s_r_ff_1_q, s_r_ff_1_qn;

  S_R_Flip_Flop s_r_ff_1 (
    .S(S), .clk(CLK), .R(R), .Q(s_r_ff_1_q), .Qn(s_r_ff_1_qn), .preset(P), .reset(_0));  // open: en
  not not_1 (not_1_out, CLK);
  // Probe on Q
  S_R_Flip_Flop s_r_ff_2 (
    .S(s_r_ff_1_q), .clk(not_1_out), .R(s_r_ff_1_qn), .Q(Q), .Qn(nQ), .reset(_0));  // open: preset, en
endmodule

module _74LS595 (
  input  nOE,
  input  RCLK,
  input  SRCLK,
  input  nSRCLR,
  input  SER,
  output A,
  output B,
  output C,
  output D,
  output E,
  output F,
  output G,
  output H,
  output nH
);

  wire d_ff_1_q, d_ff_1_qn, not_1_out, not_2_out, not_3_out, not_4_out, s_r_ff_1_q, s_r_ff_1_qn, s_r_ff_2_q,
       s_r_ff_2_qn, s_r_ff_3_q, s_r_ff_3_qn, s_r_ff_4_q, s_r_ff_4_qn, s_r_ff_5_q, s_r_ff_5_qn, s_r_ff_6_q,
       s_r_ff_6_qn, s_r_ff_7_q, s_r_ff_7_qn, s_r_ff_8_q, s_r_ff_9_q, s_r_ff_10_q, s_r_ff_11_q, s_r_ff_12_q,
       s_r_ff_13_q, s_r_ff_14_q, s_r_ff_15_q;

  not not_1 (not_1_out, nOE);
  not not_2 (not_2_out, RCLK);
  not not_3 (not_3_out, SRCLK);
  not not_4 (not_4_out, nSRCLR);
  D_Flip_Flop d_ff_1 (.clk(not_3_out), .D(SER), .Q(d_ff_1_q), .Qn(d_ff_1_qn), .reset(not_4_out));  // open: preset, en
  S_R_Flip_Flop s_r_ff_1 (
    .S(d_ff_1_q), .clk(not_3_out), .R(d_ff_1_qn), .Q(s_r_ff_1_q), .Qn(s_r_ff_1_qn), .reset(not_4_out));  // open: preset, en
  S_R_Flip_Flop s_r_ff_2 (
    .S(s_r_ff_1_q), .clk(not_3_out), .R(s_r_ff_1_qn), .Q(s_r_ff_2_q), .Qn(s_r_ff_2_qn), .reset(not_4_out));  // open: preset, en
  S_R_Flip_Flop s_r_ff_3 (
    .S(s_r_ff_2_q), .clk(not_3_out), .R(s_r_ff_2_qn), .Q(s_r_ff_3_q), .Qn(s_r_ff_3_qn), .reset(not_4_out));  // open: preset, en
  S_R_Flip_Flop s_r_ff_4 (
    .S(s_r_ff_3_q), .clk(not_3_out), .R(s_r_ff_3_qn), .Q(s_r_ff_4_q), .Qn(s_r_ff_4_qn), .reset(not_4_out));  // open: preset, en
  S_R_Flip_Flop s_r_ff_5 (
    .S(s_r_ff_4_q), .clk(not_3_out), .R(s_r_ff_4_qn), .Q(s_r_ff_5_q), .Qn(s_r_ff_5_qn), .reset(not_4_out));  // open: preset, en
  S_R_Flip_Flop s_r_ff_6 (
    .S(s_r_ff_5_q), .clk(not_3_out), .R(s_r_ff_5_qn), .Q(s_r_ff_6_q), .Qn(s_r_ff_6_qn), .reset(not_4_out));  // open: preset, en
  S_R_Flip_Flop s_r_ff_7 (
    .S(s_r_ff_6_q), .clk(not_3_out), .R(s_r_ff_6_qn), .Q(s_r_ff_7_q), .Qn(s_r_ff_7_qn), .reset(not_4_out));  // open: preset, en
  assign A = not_1_out ? s_r_ff_8_q : 1'bz;  // Controlled_Buffer controlled_buffer_1
  S_R_Flip_Flop s_r_ff_8 (.S(d_ff_1_q), .clk(not_2_out), .R(d_ff_1_qn), .Q(s_r_ff_8_q));  // open: Qn, preset, reset, en
  S_R_Flip_Flop s_r_ff_9 (
    .S(s_r_ff_1_q), .clk(not_2_out), .R(s_r_ff_1_qn), .Q(s_r_ff_9_q));  // open: Qn, preset, reset, en
  assign B = not_1_out ? s_r_ff_9_q : 1'bz;  // Controlled_Buffer controlled_buffer_2
  assign C = not_1_out ? s_r_ff_10_q : 1'bz;  // Controlled_Buffer controlled_buffer_3
  S_R_Flip_Flop s_r_ff_10 (
    .S(s_r_ff_2_q), .clk(not_2_out), .R(s_r_ff_2_qn), .Q(s_r_ff_10_q));  // open: Qn, preset, reset, en
  S_R_Flip_Flop s_r_ff_11 (
    .S(s_r_ff_3_q), .clk(not_2_out), .R(s_r_ff_3_qn), .Q(s_r_ff_11_q));  // open: Qn, preset, reset, en
  assign D = not_1_out ? s_r_ff_11_q : 1'bz;  // Controlled_Buffer controlled_buffer_4
  assign E = not_1_out ? s_r_ff_12_q : 1'bz;  // Controlled_Buffer controlled_buffer_5
  S_R_Flip_Flop s_r_ff_12 (
    .S(s_r_ff_4_q), .clk(not_2_out), .R(s_r_ff_4_qn), .Q(s_r_ff_12_q));  // open: Qn, preset, reset, en
  assign F = not_1_out ? s_r_ff_13_q : 1'bz;  // Controlled_Buffer controlled_buffer_6
  S_R_Flip_Flop s_r_ff_13 (
    .S(s_r_ff_5_q), .clk(not_2_out), .R(s_r_ff_5_qn), .Q(s_r_ff_13_q));  // open: Qn, preset, reset, en
  S_R_Flip_Flop s_r_ff_14 (
    .S(s_r_ff_6_q), .clk(not_2_out), .R(s_r_ff_6_qn), .Q(s_r_ff_14_q));  // open: Qn, preset, reset, en
  assign G = not_1_out ? s_r_ff_14_q : 1'bz;  // Controlled_Buffer controlled_buffer_7
  assign H = not_1_out ? s_r_ff_15_q : 1'bz;  // Controlled_Buffer controlled_buffer_8
  S_R_Flip_Flop s_r_ff_15 (
    .S(s_r_ff_7_q), .clk(not_2_out), .R(s_r_ff_7_qn), .Q(s_r_ff_15_q));  // open: Qn, preset, reset, en
  assign nH = not_1_out ? s_r_ff_7_q : 1'bz;  // Controlled_Buffer controlled_buffer_9
endmodule
