// Logisim project circuito-v5.2.1.circ as structural Verilog: 9 circuits, main circuit main
module main (
  input  [7:0] in_1,
  input  in_2,
  input  in_3,
  input  [7:0] in_4,
  input  in_5,
  input  in_6,
  output [7:0] out_7,
  output [7:0] out_8
);

  wire clock_1_out, clock_2_out, FIBRA1, FIBRA2, transceiver_1_load, transceiver_1_read, transceiver_2_load,
       transceiver_2_read;

  Clock clock_1 (.out(clock_1_out));
  Clock clock_2 (.out(clock_2_out));
  TRANSCEIVER transceiver_1 (
    .out_6(out_7), .in_1(in_1), .GET_IN(in_2), .SER(FIBRA2), .CLK(clock_1_out), .SH_nLD(in_3),
    .SER_OUT(FIBRA1), .LOAD(transceiver_1_load), .READ(transceiver_1_read));
  TRANSCEIVER transceiver_2 (
    .out_6(out_8), .in_1(in_4), .GET_IN(in_5), .SER(FIBRA1), .CLK(clock_2_out), .SH_nLD(in_6),
    .SER_OUT(FIBRA2), .LOAD(transceiver_2_load), .READ(transceiver_2_read));
  LED led_1 (.in(FIBRA1));
  LED led_2 (.in(transceiver_1_read));
  LED led_3 (.in(transceiver_1_load));
  LED led_4 (.in(FIBRA2));
  LED led_5 (.in(transceiver_2_read));
  LED led_6 (.in(transceiver_2_load));
  LED led_7 (.in(out_7[1]));
  LED led_8 (.in(out_7[0]));
  LED led_9 (.in(out_7[2]));
  LED led_10 (.in(out_8[0]));
  LED led_11 (.in(out_8[2]));
  LED led_12 (.in(out_8[1]));
  LED led_13 (.in(out_7[4]));
  LED led_14 (.in(out_7[3]));
  LED led_15 (.in(out_7[6]));
  LED led_16 (.in(out_7[5]));
  LED led_17 (.in(out_8[6]));
  LED led_18 (.in(out_8[5]));
  LED led_19 (.in(out_8[4]));
  LED led_20 (.in(out_8[3]));
  LED led_21 (.in(out_7[7]));
  LED led_22 (.in(out_8[7]));
endmodule

module CONTROLE (
  input  CLK,
  input  IN,
  output SHIFT,
  output LOAD
);

  wire A, B, C, D;
  wire [7:2] rom_1_data;

  Pull_Resistor pull_resistor_1 (.node(IN));
  ROM rom_1 (.addr({2'b00, A, B, C, D, IN, CLK}), .data({rom_1_data, SHIFT, LOAD}));  // open: sel
  _4520 u_4520_1 (.CLK(rom_1_data[2]), .RST(rom_1_data[3]), .D(D), .C(C), .B(B), .A(A));  // open: EN

  // Other names for the same wires on the sheet: E = IN

  // Notes on the sheet:
  //   contents of rom_1 (hex, n*v repeats v):
  //   6 6 0 6 0 6 0 6 0 6 0 6 0 6 0 6 0 6 0 6 0 6 0 6 0 6 0 6 0 6 0 6 3 7 3 7 4*e
endmodule

module EDGE (
  input  IN,
  output OUT
);

  wire not_1_out, not_2_out, not_3_out;

  Pull_Resistor pull_resistor_1 (.node(IN));
  not not_1 (not_1_out, not_2_out);
  not not_2 (not_2_out, IN);
  and and_1 (OUT, IN, not_3_out);
  not not_3 (not_3_out, not_1_out);
endmodule

module _74LS165 (
  input  A,
  input  B,
  input  C,
  input  D,
  input  E,
  input  F,
  input  G,
  input  H,
  input  SER,
  input  CLK,
  input  CLK_INH,
  input  SH_nLD,
  output Q,
  output nQ
);

  wire and_1_out, and_2_out, and_3_out, and_4_out, and_5_out, and_6_out, and_7_out, and_8_out, and_9_out,
       and_10_out, and_11_out, and_12_out, and_13_out, and_14_out, and_15_out, and_16_out, and_17_out,
       and_18_out, nor_1_out, not_1_out, not_2_out, not_3_out, not_4_out, not_5_out, not_6_out, not_7_out,
       not_8_out, not_9_out, not_10_out, not_11_out, sr_m_s_1_nq, sr_m_s_1_q, sr_m_s_2_nq, sr_m_s_2_q,
       sr_m_s_3_nq, sr_m_s_3_q, sr_m_s_4_nq, sr_m_s_4_q, sr_m_s_5_nq, sr_m_s_5_q, sr_m_s_6_nq, sr_m_s_6_q,
       sr_m_s_7_nq, sr_m_s_7_q;

  not not_1 (not_1_out, SH_nLD);
  not not_2 (not_2_out, SER);
  not not_3 (not_3_out, not_2_out);
  and and_1 (and_1_out, CLK, SH_nLD);
  nor nor_1 (nor_1_out, and_1_out, and_2_out);
  and and_2 (and_2_out, CLK_INH, SH_nLD);
  SR_M_S sr_m_s_1 (
    .S(not_3_out), .CLK(nor_1_out), .R(not_2_out), .P(and_3_out), ._0(and_4_out), .Q(sr_m_s_1_q),
    .nQ(sr_m_s_1_nq));
  not not_4 (not_4_out, and_3_out);
  and and_3 (and_3_out, A, not_1_out);
  SR_M_S sr_m_s_2 (
    .S(sr_m_s_1_q), .CLK(nor_1_out), .R(sr_m_s_1_nq), .P(and_5_out), ._0(and_6_out), .Q(sr_m_s_2_q),
    .nQ(sr_m_s_2_nq));
  and and_4 (and_4_out, not_4_out, not_1_out);
  not not_5 (not_5_out, and_5_out);
  and and_5 (and_5_out, B, not_1_out);
  SR_M_S sr_m_s_3 (
    .S(sr_m_s_2_q), .CLK(nor_1_out), .R(sr_m_s_2_nq), .P(and_7_out), ._0(and_8_out), .Q(sr_m_s_3_q),
    .nQ(sr_m_s_3_nq));
  and and_6 (and_6_out, not_5_out, not_1_out);
  not not_6 (not_6_out, and_7_out);
  and and_7 (and_7_out, C, not_1_out);
  SR_M_S sr_m_s_4 (
    .S(sr_m_s_3_q), .CLK(nor_1_out), .R(sr_m_s_3_nq), .P(and_9_out), ._0(and_10_out), .Q(sr_m_s_4_q),
    .nQ(sr_m_s_4_nq));
  and and_8 (and_8_out, not_6_out, not_1_out);
  not not_7 (not_7_out, and_9_out);
  and and_9 (and_9_out, D, not_1_out);
  SR_M_S sr_m_s_5 (
    .S(sr_m_s_4_q), .CLK(nor_1_out), .R(sr_m_s_4_nq), .P(and_11_out), ._0(and_12_out), .Q(sr_m_s_5_q),
    .nQ(sr_m_s_5_nq));
  and and_10 (and_10_out, not_7_out, not_1_out);
  not not_8 (not_8_out, and_11_out);
  and and_11 (and_11_out, E, not_1_out);
  SR_M_S sr_m_s_6 (
    .S(sr_m_s_5_q), .CLK(nor_1_out), .R(sr_m_s_5_nq), .P(and_13_out), ._0(and_14_out), .Q(sr_m_s_6_q),
    .nQ(sr_m_s_6_nq));
  and and_12 (and_12_out, not_8_out, not_1_out);
  not not_9 (not_9_out, and_13_out);
  and and_13 (and_13_out, F, not_1_out);
  SR_M_S sr_m_s_7 (
    .S(sr_m_s_6_q), .CLK(nor_1_out), .R(sr_m_s_6_nq), .P(and_15_out), ._0(and_16_out), .Q(sr_m_s_7_q),
    .nQ(sr_m_s_7_nq));
  and and_14 (and_14_out, not_9_out, not_1_out);
  not not_10 (not_10_out, and_15_out);
  and and_15 (and_15_out, G, not_1_out);
  SR_M_S sr_m_s_8 (.S(sr_m_s_7_q), .CLK(nor_1_out), .R(sr_m_s_7_nq), .P(and_17_out), ._0(and_18_out), .Q(Q), .nQ(nQ));
  and and_16 (and_16_out, not_10_out, not_1_out);
  not not_11 (not_11_out, and_17_out);
  and and_17 (and_17_out, H, not_1_out);
  and and_18 (and_18_out, not_11_out, not_1_out);
endmodule

module SR_M_S (
  input  S,
  input  CLK,
  input  R,
  input  P,
  input  _0,
  output Q,
  output nQ
);

  wire not_1_out, s_r_ff_1_q, s_r_ff_1_qn;

  S_R_Flip_Flop s_r_ff_1 (
    .S(S), .clk(CLK), .R(R), .Q(s_r_ff_1_q), .Qn(s_r_ff_1_qn), .preset(P), .reset(_0));  // open: en
  not not_1 (not_1_out, CLK);
  // Probe on Q
  S_R_Flip_Flop s_r_ff_2 (
    .S(s_r_ff_1_q), .clk(not_1_out), .R(s_r_ff_1_qn), .Q(Q), .Qn(nQ), .reset(_0));  // open: preset, en
endmodule

module _74LS595 (
  input  nOE,
  input  RCLK,
  input  SRCLK,
  input  nSRCLR,
  input  SER,
  output A,
  output B,
  output C,
  output D,
  output E,
  output F,
  output G,
  output H,
  output nH
);

  wire d_ff_1_q, d_ff_1_qn, not_1_out, not_2_out, not_3_out, not_4_out, s_r_ff_1_q, s_r_ff_1_qn, s_r_ff_2_q,
       s_r_ff_2_qn, s_r_ff_3_q, s_r_ff_3_qn, s_r_ff_4_q, s_r_ff_4_qn, s_r_ff_5_q, s_r_ff_5_qn, s_r_ff_6_q,
       s_r_ff_6_qn, s_r_ff_7_q, s_r_ff_7_qn, s_r_ff_8_q, s_r_ff_9_q, s_r_ff_10_q, s_r_ff_11_q, s_r_ff_12_q,
       s_r_ff_13_q, s_r_ff_14_q, s_r_ff_15_q;

  not not_1 (not_1_out, nOE);
  not not_2 (not_2_out, RCLK);
  not not_3 (not_3_out, SRCLK);
  not not_4 (not_4_out, nSRCLR);
  D_Flip_Flop d_ff_1 (.clk(not_3_out), .D(SER), .Q(d_ff_1_q), .Qn(d_ff_1_qn), .reset(not_4_out));  // open: preset, en
  S_R_Flip_Flop s_r_ff_1 (
    .S(d_ff_1_q), .clk(not_3_out), .R(d_ff_1_qn), .Q(s_r_ff_1_q), .Qn(s_r_ff_1_qn), .reset(not_4_out));  // open: preset, en
  S_R_Flip_Flop s_r_ff_2 (
    .S(s_r_ff_1_q), .clk(not_3_out), .R(s_r_ff_1_qn), .Q(s_r_ff_2_q), .Qn(s_r_ff_2_qn), .reset(not_4_out));  // open: preset, en
  S_R_Flip_Flop s_r_ff_3 (
    .S(s_r_ff_2_q), .clk(not_3_out), .R(s_r_ff_2_qn), .Q(s_r_ff_3_q), .Qn(s_r_ff_3_qn), .reset(not_4_out));  // open: preset, en
  S_R_Flip_Flop s_r_ff_4 (
    .S(s_r_ff_3_q), .clk(not_3_out), .R(s_r_ff_3_qn), .Q(s_r_ff_4_q), .Qn(s_r_ff_4_qn), .reset(not_4_out));  // open: preset, en
  S_R_Flip_Flop s_r_ff_5 (
    .S(s_r_ff_4_q), .clk(not_3_out), .R(s_r_ff_4_qn), .Q(s_r_ff_5_q), .Qn(s_r_ff_5_qn), .reset(not_4_out));  // open: preset, en
  S_R_Flip_Flop s_r_ff_6 (
    .S(s_r_ff_5_q), .clk(not_3_out), .R(s_r_ff_5_qn), .Q(s_r_ff_6_q), .Qn(s_r_ff_6_qn), .reset(not_4_out));  // open: preset, en
  S_R_Flip_Flop s_r_ff_7 (
    .S(s_r_ff_6_q), .clk(not_3_out), .R(s_r_ff_6_qn), .Q(s_r_ff_7_q), .Qn(s_r_ff_7_qn), .reset(not_4_out));  // open: preset, en
  S_R_Flip_Flop s_r_ff_8 (.S(d_ff_1_q), .clk(not_2_out), .R(d_ff_1_qn), .Q(s_r_ff_8_q));  // open: Qn, preset, reset, en
  assign A = not_1_out ? s_r_ff_8_q : 1'bz;  // Controlled_Buffer controlled_buffer_1
  assign B = not_1_out ? s_r_ff_9_q : 1'bz;  // Controlled_Buffer controlled_buffer_2
  S_R_Flip_Flop s_r_ff_9 (
    .S(s_r_ff_1_q), .clk(not_2_out), .R(s_r_ff_1_qn), .Q(s_r_ff_9_q));  // open: Qn, preset, reset, en
  S_R_Flip_Flop s_r_ff_10 (
    .S(s_r_ff_2_q), .clk(not_2_out), .R(s_r_ff_2_qn), .Q(s_r_ff_10_q));  // open: Qn, preset, reset, en
  assign C = not_1_out ? s_r_ff_10_q : 1'bz;  // Controlled_Buffer controlled_buffer_3
  assign D = not_1_out ? s_r_ff_11_q : 1'bz;  // Controlled_Buffer controlled_buffer_4
  S_R_Flip_Flop s_r_ff_11 (
    .S(s_r_ff_3_q), .clk(not_2_out), .R(s_r_ff_3_qn), .Q(s_r_ff_11_q));  // open: Qn, preset, reset, en
  S_R_Flip_Flop s_r_ff_12 (
    .S(s_r_ff_4_q), .clk(not_2_out), .R(s_r_ff_4_qn), .Q(s_r_ff_12_q));  // open: Qn, preset, reset, en
  assign E = not_1_out ? s_r_ff_12_q : 1'bz;  // Controlled_Buffer controlled_buffer_5
  assign F = not_1_out ? s_r_ff_13_q : 1'bz;  // Controlled_Buffer controlled_buffer_6
  S_R_Flip_Flop s_r_ff_13 (
    .S(s_r_ff_5_q), .clk(not_2_out), .R(s_r_ff_5_qn), .Q(s_r_ff_13_q));  // open: Qn, preset, reset, en
  assign G = not_1_out ? s_r_ff_14_q : 1'bz;  // Controlled_Buffer controlled_buffer_7
  S_R_Flip_Flop s_r_ff_14 (
    .S(s_r_ff_6_q), .clk(not_2_out), .R(s_r_ff_6_qn), .Q(s_r_ff_14_q));  // open: Qn, preset, reset, en
  assign H = not_1_out ? s_r_ff_15_q : 1'bz;  // Controlled_Buffer controlled_buffer_8
  S_R_Flip_Flop s_r_ff_15 (
    .S(s_r_ff_7_q), .clk(not_2_out), .R(s_r_ff_7_qn), .Q(s_r_ff_15_q));  // open: Qn, preset, reset, en
  assign nH = not_1_out ? s_r_ff_7_q : 1'bz;  // Controlled_Buffer controlled_buffer_9

  // Notes on the sheet:
  //   RCLK: pull=down
  //   nOE: pull=down
endmodule

module _74LS245 (
  input  DIR,
  input  OE,
  input  in_3,
  input  in_4,
  input  in_5,
  input  in_6,
  input  in_7,
  input  in_8,
  input  in_9,
  input  in_10,
  input  in_11,
  input  in_12,
  input  in_13,
  input  in_14,
  input  in_15,
  input  in_16,
  input  in_17,
  input  in_18,
  output out_19,
  output out_20,
  output out_21,
  output out_22,
  output out_23,
  output out_24,
  output out_25,
  output out_26,
  output out_27,
  output out_28,
  output out_29,
  output out_30,
  output out_31,
  output out_32,
  output out_33,
  output out_34
);

  wire and_1_out, and_2_out;

  and and_1 (and_1_out, ~DIR, ~OE);  // AND_Gate
  and and_2 (and_2_out, DIR, ~OE);  // AND_Gate
  assign out_19 = and_2_out ? in_3 : 1'bz;  // Controlled_Buffer controlled_buffer_1
  assign out_20 = and_1_out ? in_4 : 1'bz;  // Controlled_Buffer controlled_buffer_2
  assign out_21 = and_2_out ? in_5 : 1'bz;  // Controlled_Buffer controlled_buffer_3
  assign out_22 = and_1_out ? in_6 : 1'bz;  // Controlled_Buffer controlled_buffer_4
  assign out_23 = and_2_out ? in_7 : 1'bz;  // Controlled_Buffer controlled_buffer_5
  assign out_24 = and_1_out ? in_8 : 1'bz;  // Controlled_Buffer controlled_buffer_6
  assign out_25 = and_2_out ? in_9 : 1'bz;  // Controlled_Buffer controlled_buffer_7
  assign out_26 = and_1_out ? in_10 : 1'bz;  // Controlled_Buffer controlled_buffer_8
  assign out_27 = and_2_out ? in_11 : 1'bz;  // Controlled_Buffer controlled_buffer_9
  assign out_28 = and_1_out ? in_12 : 1'bz;  // Controlled_Buffer controlled_buffer_10
  assign out_29 = and_2_out ? in_13 : 1'bz;  // Controlled_Buffer controlled_buffer_11
  assign out_30 = and_1_out ? in_14 : 1'bz;  // Controlled_Buffer controlled_buffer_12
  assign out_31 = and_2_out ? in_15 : 1'bz;  // Controlled_Buffer controlled_buffer_13
  assign out_32 = and_1_out ? in_16 : 1'bz;  // Controlled_Buffer controlled_buffer_14
  assign out_33 = and_2_out ? in_17 : 1'bz;  // Controlled_Buffer controlled_buffer_15
  assign out_34 = and_1_out ? in_18 : 1'bz;  // Controlled_Buffer controlled_buffer_16
endmodule

module TRANSCEIVER (
  input  [7:0] in_1,
  input  GET_IN,
  input  SER,
  input  CLK,
  input  SH_nLD,
  output [7:0] out_6,
  output LOAD,
  output SER_OUT,
  output READ
);

  wire controle_1_shift, d_ff_1_qn, n74ls245_1_out_19, n74ls245_1_out_21, n74ls245_1_out_23,
       n74ls245_1_out_25, n74ls245_1_out_27, n74ls245_1_out_29, n74ls245_1_out_31, n74ls245_1_out_33;
  wire [1:1] rom_1_data;
  wire [2:2] n4520_1_a;

  CONTROLE controle_1 (.CLK(CLK), .IN(SER), .LOAD(LOAD), .SHIFT(controle_1_shift));
  _74LS245 u_74ls245_1 (
    .DIR(GET_IN), .OE(1'b0), .in_3(in_1[0]), .out_20(out_6[0]), .in_4(n74ls245_1_out_19),
    .out_19(n74ls245_1_out_19), .in_5(in_1[1]), .out_21(n74ls245_1_out_21), .out_22(out_6[1]),
    .in_6(n74ls245_1_out_21), .in_7(in_1[2]), .out_23(n74ls245_1_out_23), .out_24(out_6[2]),
    .in_8(n74ls245_1_out_23), .in_9(in_1[3]), .out_25(n74ls245_1_out_25), .out_26(out_6[3]),
    .in_10(n74ls245_1_out_25), .in_11(in_1[4]), .out_27(n74ls245_1_out_27), .out_28(out_6[4]),
    .in_12(n74ls245_1_out_27), .in_13(in_1[5]), .out_29(n74ls245_1_out_29), .out_30(out_6[5]),
    .in_14(n74ls245_1_out_29), .in_15(in_1[6]), .out_31(n74ls245_1_out_31), .out_32(out_6[6]),
    .in_16(n74ls245_1_out_31), .in_17(in_1[7]), .out_33(n74ls245_1_out_33), .out_34(out_6[7]),
    .in_18(n74ls245_1_out_33));
  _74LS595 u_74ls595_1 (
    .nOE(GET_IN), .RCLK(LOAD), .SRCLK(controle_1_shift), .nSRCLR(1'b1), .SER(SER), .A(n74ls245_1_out_19),
    .B(n74ls245_1_out_21), .C(n74ls245_1_out_23), .D(n74ls245_1_out_25), .E(n74ls245_1_out_27),
    .F(n74ls245_1_out_29), .G(n74ls245_1_out_31), .H(n74ls245_1_out_33));  // open: nH
  Pull_Resistor pull_resistor_1 (.node(READ));
  ROM #(.addrWidth(3), .dataWidth(2)) rom_1 (
    .addr({n4520_1_a[2], SH_nLD, READ}), .data({rom_1_data[1], READ}));  // open: sel
  _4520 u_4520_1 (.CLK(CLK), .RST(READ), .A(n4520_1_a[2]), .EN(rom_1_data[1]));  // open: D, C, B
  _74LS165 u_74ls165_1 (
    .SER(1'b0), .CLK(CLK), .CLK_INH(1'b0), .SH_nLD(SH_nLD), .Q(SER_OUT), .A(n74ls245_1_out_19),
    .B(n74ls245_1_out_21), .C(n74ls245_1_out_23), .D(n74ls245_1_out_25), .E(n74ls245_1_out_27),
    .F(n74ls245_1_out_29), .G(n74ls245_1_out_31), .H(n74ls245_1_out_33));  // open: nQ
  D_Flip_Flop d_ff_1 (.clk(n4520_1_a[2]), .D(d_ff_1_qn), .Qn(d_ff_1_qn));  // open: Q, preset, en, reset

  // Notes on the sheet:
  //   contents of rom_1 (hex, n*v repeats v):
  //   0 0 2 1 0 0 1 1
endmodule

module _4520 (
  input  CLK,
  input  RST,
  input  EN,
  output D,
  output C,
  output B,
  output A
);

  wire d_ff_1_qn, d_ff_2_qn, d_ff_3_qn, d_ff_4_qn;

  D_Flip_Flop d_ff_1 (.clk(CLK), .D(d_ff_1_qn), .Q(D), .Qn(d_ff_1_qn), .en(EN), .reset(RST));  // open: preset
  D_Flip_Flop d_ff_2 (.clk(d_ff_1_qn), .D(d_ff_2_qn), .Q(C), .Qn(d_ff_2_qn), .en(EN), .reset(RST));  // open: preset
  D_Flip_Flop d_ff_3 (.clk(d_ff_2_qn), .D(d_ff_3_qn), .Q(B), .Qn(d_ff_3_qn), .en(EN), .reset(RST));  // open: preset
  D_Flip_Flop d_ff_4 (.clk(d_ff_3_qn), .D(d_ff_4_qn), .Q(A), .Qn(d_ff_4_qn), .en(EN), .reset(RST));  // open: preset
endmodule
